# Fritzing sketch RECEIVER SCHEMA ELECTRIQUE (saved by Fritzing 0.9.3b)
breadboards: 1

parts:
  Composant1 = Arduino Nano (Rev3.0)
  S1 = Pushbutton [package="[THT]"]
  Composant2 = NRF24L01+ Breakout Board
  R1 = Resistor [tolerance=±5% resistance=220 package="0603 [SMD]"]

nets:
  N1: Composant1.D6, Composant2.SCK
  N2: Composant1.D7, Composant2.CE
  N3: Composant1.D8, Composant2.CS
  N4: Composant1.D11/MOSI, Composant2.MOSI
  N5: Composant1.D12/MISO, Composant2.MISO
  GND: Composant1.GND, Composant2.GND, R1.Pin_1
  3V3: Composant1.3V3, S1.Pin_3, S1.Pin_4, Composant2.VCC
  N6: S1.Pin_1, S1.Pin_2, R1.Pin_0
