# Fritzing sketch SCHEMA ELECTRIQUE V2 (saved by Fritzing 0.9.3b)
breadboards: 1

parts:
  Composant1 = Arduino Mega 2560 (Rev3)-TopMount
  M1 = DC Motor  # not connected
  M2 = DC Motor  # not connected
  L298N1 = L298N DC motor driver
  BATT1 = LiPoly Battery (1300mAh)
  M7 = DC Motor  # not connected
  M8 = DC Motor  # not connected
  L298N4 = L298N DC motor driver
  M9 = DC Motor  # not connected
  M10 = DC Motor  # not connected
  L298N5 = L298N DC motor driver
  J1 = Basic Servo

nets:
  N1: Composant1.A0, J1.pulse
  GND: Composant1.GND, L298N1.GND, BATT1.negative, L298N4.GND, L298N5.GND, J1.gnd
  N2: Composant1.D24, L298N4.ENB
  N3: Composant1.D25, L298N5.ENA
  N4: Composant1.D26, L298N4.IN4
  N5: Composant1.D27, L298N5.IN1
  N6: Composant1.D28, L298N4.IN3
  N7: Composant1.D29, L298N5.IN2
  N8: Composant1.D30, L298N4.IN2
  N9: Composant1.D31, L298N5.IN3
  N10: Composant1.D32, L298N4.IN1
  N11: Composant1.D33, L298N5.IN4
  N12: Composant1.D34, L298N4.ENA
  N13: Composant1.D35, L298N5.ENB
  N14: Composant1.D36, L298N1.ENB
  N15: Composant1.D38, L298N1.IN4
  N16: Composant1.D40, L298N1.IN3
  N17: Composant1.D42, L298N1.IN2
  N18: Composant1.D44, L298N1.IN1
  N19: Composant1.D46, L298N1.ENA
  12V: L298N1.12V, BATT1.positive, J1.vcc

custom parts:
  Arduino Mega 2560 (Rev3)-TopMount: Arduino Mega 2560 (Rev3) for Top PCB Mount. The PCB view of the Arduino Mega 2560 (Rev3) in Arduino Bin flipped upside down with the text flipped back so as to be readable. Other views haven't changed Protruding component position is outlined to provide indication of part contact. Number in component outline is mm of protrusion of the component from the Mega PCB. Subtract the number from the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
  L298N DC motor driver: 2x DC motor driver with 78M05 positive voltage regulator (7..35 V) L298N: max 46 V, 2 A Set 5 V Enable jumper to enable 5 V regultor (needed for the L298N) and +5 V output at screw terminal or supply external +5 V at screw terminal Set ENA and/or ENB to +5 V to enable motor permanently or supply ENA and/or ENB with PWM signal IN1 and IN2 set rotation directory for motor A (OUT1/OUT2) IN2 and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
  LiPoly Battery (1300mAh): Lithium Ion Polymer Battery (1300mAh)
