# Fritzing sketch Schéma électrique (saved by Fritzing 0.9.3b)
breadboards: 1

parts:
  Composant1 = NRF24L01+ Breakout Board  # not connected
  Composant2 = NRF24L01+ Breakout Board
  Composant3 = Arduino Mega 2560 (Rev3)
  M1 = DC Motor  # not connected
  M2 = DC Motor
  U2 = LIPO-2000mAh [package=lipo-2000]
  ANT1 = Antenna
  J1 = Basic Servo
  Composant6 = Arduino Nano (Rev3.0) (ICSP)
  M3 = DC Motor  # not connected
  M4 = DC Motor  # not connected
  L298N1 = L298N DC motor driver
  U3 = L9110 H-bridge module [part_number="L9110 H-bridge"]
  U4 = L9110 H-bridge module [part_number="L9110 H-bridge"]
  U5 = L9110 H-bridge module [part_number="L9110 H-bridge"]
  U6 = L9110 H-bridge module [part_number="L9110 H-bridge"]
  M5 = DC Motor
  M6 = DC Motor
  M7 = DC Motor
  M8 = DC Motor
  Composant7 = Thumb Joystick

nets:
  GND: Composant2.GND, Composant6.GND, Composant7.GND
  VCC: Composant2.VCC, Composant6.5V, Composant7.VCC
  N1: Composant2.CE, Composant6.D9
  N2: Composant2.CS, Composant6.D8
  N3: Composant2.SCK, Composant6.D10
  N4: Composant2.MOSI, Composant6.D7
  N5: Composant2.MISO, Composant6.D11/MOSI
  N6: Composant2.IRQ, Composant6.D6
  GND_2: Composant3.GND, J1.gnd, L298N1.GND, U3.GND, U4.GND, U5.GND, U6.GND
  5V: Composant3.5V, J1.vcc
  N7: Composant3.D3_PWM, J1.pulse
  N8: Composant3.D22, U3.A-IB
  N9: Composant3.D24, U3.A-IA
  N10: Composant3.D32, U4.A-IB
  N11: Composant3.D34, U4.A-IA
  N12: Composant3.D42, U5.A-IB
  N13: Composant3.D45, L298N1.IN1
  N14: Composant3.D46, U5.A-IA
  N15: Composant3.D47, L298N1.IN2
  N16: Composant3.D49, L298N1.IN3
  N17: Composant3.D50, U6.A-IB
  N18: Composant3.D51, L298N1.IN4
  N19: Composant3.D52, U6.A-IA
  N20: M2.pin_1, ANT1.antenna_lead
  VCC_2: U2.+, L298N1.12V, U3.VCC, U4.VCC, U5.VCC, U6.VCC
  N21: Composant6.D5, Composant7.SEL
  N22: Composant6.A1, Composant7.HORZ
  N23: Composant6.A0, Composant7.VERT
  N24: U3.MOTOR_A-A, M5.pin_2
  N25: U3.MOTOR_A-B, M5.pin_1
  N26: U4.MOTOR_A-A, M6.pin_2
  N27: U4.MOTOR_A-B, M6.pin_1
  N28: U5.MOTOR_A-A, M7.pin_2
  N29: U5.MOTOR_A-B, M7.pin_1
  N30: U6.MOTOR_A-A, M8.pin_2
  N31: U6.MOTOR_A-B, M8.pin_1

notes:
  Treuil M2
  Treuil M1
  Vérins
  Vérin Mât M4
  Vérin mat de grande vergue M3
  Vérin de la croix X2 M6 et M7
  MB : Moteurs Brushless

custom parts:
  L298N DC motor driver: 2x DC motor driver with 78M05 positive voltage regulator (7..35 V) L298N: max 46 V, 2 A Set 5 V Enable jumper to enable 5 V regultor (needed for the L298N) and +5 V output at screw terminal or supply external +5 V at screw terminal Set ENA and/or ENB to +5 V to enable motor permanently or supply ENA and/or ENB with PWM signal IN1 and IN2 set rotation directory for motor A (OUT1/OUT2) IN2 and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

// code stored in the sketch: Untitled2.ino
void setup()
{
  pinMode(7, OUTPUT);
}

void loop()
{
  analogWrite(7, 0);
  delay(1000); // Wait for 1000 millisecond(s)
  analogWrite(7,127);
  delay(1000);
  analogWrite(7, 255);
  delay(1000); // Wait for 1000 millisecond(s)
}
